# Fritzing sketch pwmTOpwm (saved by Fritzing 0.9.3b)
breadboards: 1

parts:
  Part1 = Arduino Nano (Rev3.0)
  R1 = Resistor [tolerance=±5% resistance=10k package=THT]
  R2 = Trimmer Potentiometer [maximum_resistance=10kΩ package=THT]  # not connected

nets:
  N1: Part1.GND, R1.Pin_0
  N2: Part1.A1, R1.Pin_1

notes:
  PWM_IN
  PWM_OUT
  SDA
  SCL
  PWMtoPWM: https://github.com/DaveCalaway/PWMtoPWM
