# Fritzing sketch pwmTOpwm+laser (saved by Fritzing 0.9.3b)
breadboards: 1

parts:
  Part1 = Arduino Nano (Rev3.0)
  R1 = Resistor [tolerance=±5% resistance=10k package=THT]
  RE1 = Rotary Encoder [package=THT]
  R2 = Resistor [tolerance=±5% resistance=10k package=THT]
  R3 = Resistor [tolerance=±5% resistance=10k package=THT]
  Part2 = Arduino Nano (Rev3.0)  # not connected

nets:
  N1: Part1.GND, R1.Pin_0, RE1.EncoderPinC
  N2: Part1.D2, RE1.EncoderPinB, R2.Pin_1
  N3: Part1.D3, RE1.EncoderPinA, R3.Pin_1
  N4: Part1.5V, R2.Pin_0, R3.Pin_0
  N5: Part1.A1, R1.Pin_1

notes:
  PWM_IN
  PWM_OUT
  SDA
  SCL
  PWMtoPWM_dual: https://goo.gl/g1ChXk
  Trimmer button pins
  Laser Simulator
